// Logisim project circuit.circ as structural Verilog
// NOT
module _74HC04 (
  input  _1A,
  input  Vcc,
  input  _6A,
  input  _2A,
  input  _5A,
  input  _3A,
  input  _4A,
  input  GND,
  output _1Y,
  output _6Y,
  output _2Y,
  output _5Y,
  output _3Y,
  output _4Y
);

  not not_1 (_1Y, _1A);
  not not_2 (_2Y, _2A);
  not not_3 (_3Y, _3A);
  not not_4 (_6Y, _6A);
  not not_5 (_5Y, _5A);
  not not_6 (_4Y, _4A);
endmodule

// AND
module _74HC08 (
  input  _1A,
  input  Vcc,
  input  _1B,
  input  _4A,
  input  _4B,
  input  _2A,
  input  _2B,
  input  _3A,
  input  _3B,
  input  GND,
  output _1Y,
  output _4Y,
  output _2Y,
  output _3Y
);

  and and_1 (_1Y, _1B, _1A);
  and and_2 (_4Y, _4A, _4B);
  and and_3 (_2Y, _2B, _2A);
  and and_4 (_3Y, _3A, _3B);
endmodule

// OR
module _74HC32 (
  input  _1A,
  input  Vcc,
  input  _1B,
  input  _4A,
  input  _4B,
  input  _2A,
  input  _2B,
  input  _3A,
  input  _3B,
  input  GND,
  output _1Y,
  output _4Y,
  output _2Y,
  output _3Y
);

  or or_1 (_1Y, _1B, _1A);
  or or_2 (_4Y, _4A, _4B);
  or or_3 (_2Y, _2B, _2A);
  or or_4 (_3Y, _3A, _3B);
endmodule

// NAND
module _74HC00 (
  input  _1A,
  input  Vcc,
  input  _1B,
  input  _4A,
  input  _4B,
  input  _2A,
  input  _2B,
  input  _3A,
  input  _3B,
  input  GND,
  output _1Y,
  output _4Y,
  output _2Y,
  output _3Y
);

  nand nand_1 (_1Y, _1B, _1A);
  nand nand_2 (_4Y, _4A, _4B);
  nand nand_3 (_2Y, _2B, _2A);
  nand nand_4 (_3Y, _3A, _3B);
endmodule

module Decoder (
  input  op0,
  input  op1,
  input  op2,
  input  op3,
  input  C_Flag,
  output SELECT_B,
  output SELECT_A,
  output LOAD_0,
  output LOAD_1,
  output LOAD_2,
  output LOAD_3
);

  wire n74hc10_1__3y, n74hc32_1__4y, not_1_out;

  not not_1 (not_1_out, C_Flag);
  _74HC32 u_74hc32_1 (
    ._1A(op2), ._1B(op3), ._1Y(LOAD_0), ._2A(op0), ._2B(op3), ._2Y(SELECT_A), ._4A(not_1_out), ._4B(op0),
    ._4Y(n74hc32_1__4y), ._3A(n74hc10_1__3y), ._3B(op3), ._3Y(LOAD_1));  // open: GND, Vcc
  _74HC10 u_74hc10_1 (
    ._1A(op3), ._1B(n74hc10_1__3y), ._2A(n74hc32_1__4y), ._2B(op2), ._2C(op3), ._2Y(LOAD_3), ._1C(1'b1),
    ._1Y(LOAD_2), ._3C(1'b1), ._3B(1'b1), ._3A(op2), ._3Y(n74hc10_1__3y));  // open: GND, Vcc

  assign SELECT_B = op1;
endmodule

// NAND_3
module _74HC10 (
  input  _1A,
  input  Vcc,
  input  _1B,
  input  _1C,
  input  _2A,
  input  _2B,
  input  _3C,
  input  _2C,
  input  _3B,
  input  _3A,
  input  GND,
  output _1Y,
  output _2Y,
  output _3Y
);

  nand nand_1 (_1Y, _1B, _1A, _1C);
  nand nand_2 (_2Y, _2C, _2B, _2A);
  nand nand_3 (_3Y, _3C, _3B, _3A);
endmodule

module _74HC153 (
  input  _1_nG,
  input  Vcc,
  input  B,
  input  _2_nG,
  input  _1C3,
  input  A,
  input  _1C2,
  input  _2C3,
  input  _1C1,
  input  _2C2,
  input  _1C0,
  input  _2C1,
  input  _2C0,
  input  GND,
  output _1Y,
  output _2Y
);

  Multiplexer multiplexer_1 ();  // open: in0, in1, out, sel, en
endmodule

module MUX (
  input  in_1,
  input  in_2,
  input  in_3,
  input  in_4,
  input  in_5
);
endmodule
